# Fritzing sketch Platine (saved by Fritzing 0.9.9b)
breadboards: 1

parts:
  Raspberry_Pi_1 = Raspberry Pi 3 [part_number=RPI-3-V1.2]
  J1 = Basic Servo
  LED1 = RGB LED (com. cathode, rgb) [package="5 mm [THT]"]

nets:
  N1: Raspberry_Pi_1.GPIO17, J1.pulse
  N2: Raspberry_Pi_1.GPIO10, LED1.red_anode
  5V: Raspberry_Pi_1.5V, J1.vcc
